# Fritzing sketch Elek-mer-projekts (saved by Fritzing 0.9.10b)
breadboards: 1

parts:
  LED1 = LED - 3mm [color="Red (633nm)" current=0.030 package="3 mm [THT]"]
  U1 = ESP32S-HiLetgo [part_number=ESP32S-HiLetgo]
  S1 = Pushbutton [package="[THT]"]
  D3 = Diode [package=diode-1n4148]
  R3 = Resistor [tolerance=±5% resistance=5.1 package="0402 [SMD]"]
  R4 = Resistor [tolerance=±5% resistance=4.7 power=2W package="0402 [SMD]"]
  R5 = Resistor [tolerance=±5% resistance=4.7 power=2W package="0402 [SMD]"]
  R6 = Resistor [tolerance=±5% resistance=4.7 power=2W package="0402 [SMD]"]
  R7 = Resistor [tolerance=±5% resistance=4.7 power=2W package="0402 [SMD]"]
  R8 = Resistor [tolerance=±5% resistance=5.1 package="0402 [SMD]"]
  D11 = Diode [package=diode-1n4148]
  D12 = Diode [package=diode-1n4148]
  D13 = Diode [package=diode-1n4148]
  D14 = Diode [package=diode-1n4148]
  D15 = Diode [package=diode-1n4148]
  D16 = Diode [package=diode-1n4148]
  D17 = Diode [package=diode-1n4148]
  R9 = Resistor [tolerance=±5% resistance=100k package="0402 [SMD]"]
  R10 = Resistor [tolerance=±5% resistance=1800k package="0402 [SMD]"]
  R11 = Resistor [tolerance=±5% resistance=1800k package="0402 [SMD]"]
  R12 = Resistor [tolerance=±5% resistance=1k power=1W package="0402 [SMD]"]
  R13 = Resistor [tolerance=±5% resistance=1k power=1W package="0402 [SMD]"]
  R14 = Resistor [tolerance=±5% resistance=100k package="0402 [SMD]"]
  R15 = Resistor [tolerance=±5% resistance=1800k package="0402 [SMD]"]
  R16 = Resistor [tolerance=±5% resistance=1800k package="0402 [SMD]"]

nets:
  N1: LED1.cathode, U1.GND, S1.Pin_1, S1.Pin_2, D3.A, D13.A, D16.A, D17.A, R9.Pin_0, R14.Pin_0
  N2: U1.GPIO32, R9.Pin_1, R10.Pin_0, R11.Pin_0
  N3: U1.GPIO33, R14.Pin_1, R15.Pin_0, R16.Pin_0
  N4: U1.GPIO16, R12.Pin_0
  N5: U1.GPIO17, R13.Pin_1
  N6: S1.Pin_3, R13.Pin_0
  N7: D3.C, R3.Pin_1, R4.Pin_1, R5.Pin_1, R6.Pin_1, R7.Pin_1, R8.Pin_1, D11.A
  N8: R3.Pin_0, R4.Pin_0, R5.Pin_0, R6.Pin_0, R7.Pin_0, R8.Pin_0, D14.A, D17.C
  N9: D11.C, D12.C, R15.Pin_1, R16.Pin_1
  N10: D12.A, D13.C, D15.A, D16.C
  N11: D14.C, D15.C, R10.Pin_1, R11.Pin_1

notes:
  Supply+ Probe
  Voltmeter 1
  Supply- Probe
  Load- Probe
  Load+ Probe
  Voltmeter 2

custom parts:
  ESP32S-HiLetgo: HiLetgo ESP-WROOM-32 ESP32 ESP-32S Development Board 2.4GHz Dual-Mode WiFi + Bluetooth Dual Cores Microcontroller The ESP32 integrated with Antenna switches, RF Balun, power amplifiers, low-noise amplifiers, filters, and management modules, and the entire solution occupies the least area of PCB. 2.4 GHz Wi-Fi plus Bluetooth dual-mode chip, with TSMC Ultra-low power consumption 40nm technology,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
